// Digital circuit ProjectCPUdiglo.dig as structural Verilog
module ProjectCPUdiglo (
  input  [7:0] M,
  input  [7:0] N,
  input  [12:0] progIN,
  input  reset,
  input  progLoad,
  input  start,
  input  result,
  input  clk,
  output valid,
  output done,
  output [7:0] \output ,
  output [12:0] out_12,
  output [12:0] out_13,
  output [4:0] out_14,
  output [7:0] out_15,
  output [7:0] out_16,
  output [7:0] out_17,
  output [4:0] out_18,
  output GCDbusy,
  output [7:0] GCD,
  output [15:0] LCM
);

  wire _0, _1, _2, _3, _4, _5, _6, _7, _8, _9, _10, _11, _12, _13, _14, _15, _16, _17, _18, _19, _20, _21,
       _22, _23, _24, _25, _26, _27, _28, _29, _30, accA_set2, accA_set3, accA_set4, accA_set5, and_1_out,
       and_2_out, and_3_out, and_4_out, and_5_out, and_6_out, and_7_out, and_8_out, and_9_out, and_10_out,
       and_11_out, and_12_out, and_15_out, comparator_1_gt, comparator_3_eq, comparator_8_gt,
       comparator_9_eq, comparator_10_gt, comparator_12_eq, comparator_12_gt, comparator_13_eq,
       counter_1_out, ENABLE_LCD1, ENABLE_LCD2, ENABLE_M, ENABLE_N, ENABLE_PC, ENABLE_reset, EQ, eq_t,
       finalresult, GT, gt_t, isprime, Jump_PC, LE, le_t, LOAD_A, LOAD_B, LOAD_C, load_done,
       multiplexer_28_out, or_1_out, or_2_out, or_3_out, or_4_out, or_5_out, or_8_out, or_11_out, or_13_out,
       or_15_out, or_21_out, or_24_out, or_26_out, or_27_out, prime, regC_set2, register_1_q, register_3_q,
       rRAM_read;
  wire [7:0] add, add_1_s, add_2_s, add_3_s, add_4_s, ALU, \and , counter_2_out, counter_3_out,
       counter_4_out, divide, GCD_PC, LCM_PC, MM, mod, mul, multiplexer_2_out, multiplexer_3_out,
       multiplexer_4_out, multiplexer_5_out, multiplexer_6_out, multiplexer_7_out, multiplexer_8_out,
       multiplexer_9_out, multiplexer_10_out, multiplexer_11_out, multiplexer_12_out, multiplexer_14_out,
       multiplexer_15_out, multiplexer_16_out, multiplexer_17_out, multiplexer_18_out, multiplexer_19_out,
       multiplexer_20_out, multiplexer_21_out, multiplexer_22_out, multiplexer_23_out, multiplexer_24_out,
       multiplexer_25_out, multiplexer_26_out, multiplexer_27_out, NN, \not , operand, operand_copy, \or ,
       power, register_4_q, register_6_q, register_7_q, rRAM, rRAM_PC, shift, sub, sub_1_s, sub_2_s, \xor ;
  wire [15:0] mul_2_mul;

  Multiplexer #(.Selector_Bits(8)) multiplexer_1 (
    .sel(out_15), .in_0(1'b0), .in_1(1'b0), .in_2(1'b1), .in_3(1'b1), .in_4(1'b0), .in_5(1'b1), .in_6(1'b0),
    .in_7(1'b1), .in_8(1'b0), .in_9(1'b0), .in_10(1'b0), .in_11(1'b1), .in_12(1'b0), .in_13(1'b1),
    .in_14(1'b0), .in_15(1'b0), .in_16(1'b0), .in_17(1'b1), .in_18(1'b0), .in_19(1'b1), .in_20(1'b0),
    .in_21(1'b0), .in_22(1'b0), .in_23(1'b1), .in_24(1'b0), .in_25(1'b0), .in_26(1'b0), .in_27(1'b0),
    .in_28(1'b0), .in_29(1'b1), .in_30(1'b0), .in_31(1'b1), .in_32(1'b0), .in_33(1'b0), .in_34(1'b0),
    .in_35(1'b0), .in_36(1'b0), .in_37(1'b1), .in_38(1'b0), .in_39(1'b0), .in_40(1'b0), .in_41(1'b1),
    .in_42(1'b0), .in_43(1'b1), .in_44(1'b0), .in_45(1'b0), .in_46(1'b0), .in_47(1'b1), .in_48(1'b0),
    .in_49(1'b0), .in_50(1'b0), .in_51(1'b0), .in_52(1'b0), .in_53(1'b1), .in_54(1'b0), .in_55(1'b0),
    .in_56(1'b0), .in_57(1'b0), .in_58(1'b0), .in_59(1'b1), .in_60(1'b0), .in_61(1'b1), .in_62(1'b0),
    .in_63(1'b0), .in_64(1'b0), .in_65(1'b0), .in_66(1'b0), .in_67(1'b1), .in_68(1'b0), .in_69(1'b0),
    .in_70(1'b0), .in_71(1'b1), .in_72(1'b0), .in_73(1'b1), .in_74(1'b0), .in_75(1'b0), .in_76(1'b0),
    .in_77(1'b0), .in_78(1'b0), .in_79(1'b1), .in_80(1'b0), .in_81(1'b0), .in_82(1'b0), .in_83(1'b1),
    .in_84(1'b0), .in_85(1'b0), .in_86(1'b0), .in_87(1'b0), .in_88(1'b0), .in_89(1'b1), .in_90(1'b0),
    .in_91(1'b0), .in_92(1'b0), .in_93(1'b0), .in_94(1'b0), .in_95(1'b0), .in_96(1'b0), .in_97(1'b1),
    .in_98(1'b0), .in_99(1'b0), .in_100(1'b0), .in_101(1'b1), .in_102(1'b0), .in_103(1'b1), .in_104(1'b0),
    .in_105(1'b0), .in_106(1'b0), .in_107(1'b1), .in_108(1'b0), .in_109(1'b1), .in_110(1'b0), .in_111(1'b0),
    .in_112(1'b0), .in_113(1'b1), .in_114(1'b0), .in_115(1'b0), .in_116(1'b0), .in_117(1'b0), .in_118(1'b0),
    .in_119(1'b0), .in_120(1'b0), .in_121(1'b0), .in_122(1'b0), .in_123(1'b0), .in_124(1'b0), .in_125(1'b0),
    .in_126(1'b0), .in_127(1'b1), .in_128(1'b0), .in_129(1'b0), .in_130(1'b0), .in_131(1'b1), .in_132(1'b0),
    .in_133(1'b0), .in_134(1'b0), .in_135(1'b0), .in_136(1'b0), .in_137(1'b1), .in_138(1'b0), .in_139(1'b1),
    .in_140(1'b0), .in_141(1'b0), .in_142(1'b0), .in_143(1'b0), .in_144(1'b0), .in_145(1'b0), .in_146(1'b0),
    .in_147(1'b0), .in_148(1'b0), .in_149(1'b1), .in_150(1'b0), .in_151(1'b1), .in_152(1'b0), .in_153(1'b0),
    .in_154(1'b0), .in_155(1'b0), .in_156(1'b0), .in_157(1'b1), .in_158(1'b0), .in_159(1'b0), .in_160(1'b0),
    .in_161(1'b0), .in_162(1'b0), .in_163(1'b1), .in_164(1'b0), .in_165(1'b0), .in_166(1'b0), .in_167(1'b1),
    .in_168(1'b0), .in_169(1'b0), .in_170(1'b0), .in_171(1'b0), .in_172(1'b0), .in_173(1'b1), .in_174(1'b0),
    .in_175(1'b0), .in_176(1'b0), .in_177(1'b0), .in_178(1'b0), .in_179(1'b1), .in_180(1'b0), .in_181(1'b1),
    .in_182(1'b0), .in_183(1'b0), .in_184(1'b0), .in_185(1'b0), .in_186(1'b0), .in_187(1'b0), .in_188(1'b0),
    .in_189(1'b0), .in_190(1'b0), .in_191(1'b1), .in_192(1'b0), .in_193(1'b1), .in_194(1'b0), .in_195(1'b0),
    .in_196(1'b0), .in_197(1'b1), .in_198(1'b0), .in_199(1'b1), .in_200(1'b0), .in_201(1'b0), .in_202(1'b0),
    .in_203(1'b0), .in_204(1'b0), .in_205(1'b0), .in_206(1'b0), .in_207(1'b0), .in_208(1'b0), .in_209(1'b0),
    .in_210(1'b0), .in_211(1'b1), .in_212(1'b0), .in_213(1'b0), .in_214(1'b0), .in_215(1'b0), .in_216(1'b0),
    .in_217(1'b0), .in_218(1'b0), .in_219(1'b0), .in_220(1'b0), .in_221(1'b0), .in_222(1'b0), .in_223(1'b1),
    .in_224(1'b0), .in_225(1'b0), .in_226(1'b0), .in_227(1'b1), .in_228(1'b0), .in_229(1'b1), .in_230(1'b0),
    .in_231(1'b0), .in_232(1'b0), .in_233(1'b1), .in_234(1'b0), .in_235(1'b0), .in_236(1'b0), .in_237(1'b0),
    .in_238(1'b0), .in_239(1'b1), .in_240(1'b0), .in_241(1'b1), .in_242(1'b0), .in_243(1'b0), .in_244(1'b0),
    .in_245(1'b0), .in_246(1'b0), .in_247(1'b0), .in_248(1'b0), .in_249(1'b0), .in_250(1'b0), .in_251(1'b1),
    .in_252(1'b0), .in_253(1'b0), .in_254(1'b0), .in_255(1'b0), .out(prime));
  or or_1 (or_1_out, start, valid);
  Comparator #(.Bits(8)) comparator_1 (.a(LCM_PC), .b(8'h1), .gt(comparator_1_gt));  // open: eq, lt
  or or_2 (or_2_out, _10, _9);
  Decoder #(.Selector_Bits(5)) decoder_1 (
    .sel(out_18), .out_0(_0), .out_1(_1), .out_2(_2), .out_3(_3), .out_4(_4), .out_5(_5), .out_6(_6),
    .out_7(_7), .out_8(_8), .out_9(_9), .out_10(_10), .out_11(_11), .out_12(_12), .out_13(_13), .out_14(_14),
    .out_15(_15), .out_16(_16), .out_17(_17), .out_18(_18), .out_19(_19), .out_20(_20), .out_21(_21),
    .out_22(_22), .out_23(_23), .out_24(_24), .out_25(_25), .out_26(_26), .out_27(_27), .out_28(_28),
    .out_29(_29), .out_30(_30), .out_31(valid));
  Register register_1 (.D(start), .C(clk), .en(or_1_out), .Q(register_1_q));
  or or_3 (or_3_out, ~_30, comparator_1_gt);  // Or
  and and_1 (and_1_out, _10, _9, ~start);  // And
  Counter counter_1 (.en(or_2_out), .C(clk), .clr(ENABLE_PC), .out(counter_1_out));  // open: ovf
  Comparator comparator_2 (.a(counter_1_out), .b(1'b1), .eq(load_done));  // open: gt, lt
  and and_2 (and_2_out, register_1_q, ~valid, or_3_out);  // And
  or or_4 (or_4_out, ~and_1_out, load_done);  // Or
  or or_5 (or_5_out, ~and_1_out, load_done);  // Or
  or or_6 (LOAD_A, _1, _28, _27, _26, _25, _24, _22, _21, _22, _20, _19, _18, _17, _9, _3, _6, _10);
  or or_7 (accA_set4, _3, _28, _27, _26, _25, _24, _23, _22, _21, _20, _19, _18, _17, _10, _6, _29);
  or or_8 (or_8_out, result, reset);
  or or_9 (accA_set5, accA_set4, _9);
  Register register_2 (.D(result), .C(clk), .en(or_8_out), .Q(finalresult));
  and and_3 (and_3_out, and_2_out, or_4_out, or_5_out);
  or or_10 (ENABLE_PC, and_3_out, reset);
  Comparator #(.Bits(8)) comparator_3 (.a(LCM_PC), .b({8{1'b0}}), .eq(comparator_3_eq));  // open: gt, lt
  Comparator #(.Bits(8)) comparator_4 (.a(LCM_PC), .b(8'h1), .eq(ENABLE_LCD2));  // open: gt, lt
  Comparator #(.Bits(8)) comparator_5 (.a(GCD_PC), .b(8'h1), .eq(ENABLE_M));  // open: gt, lt
  Comparator #(.Bits(8)) comparator_6 (.a(GCD_PC), .b(8'h2), .eq(ENABLE_N));  // open: gt, lt
  or or_11 (or_11_out, result, reset);
  Counter #(.Bits(8)) counter_2 (.en(finalresult), .C(clk), .clr(or_11_out), .out(counter_2_out));  // open: ovf
  and and_4 (and_4_out, _30, comparator_3_eq);
  or or_12 (rRAM_read, _30, _10);
  Multiplexer #(.Bits(8)) multiplexer_2 (.sel(Jump_PC), .in_0(add_1_s), .in_1(operand), .out(multiplexer_2_out));
  or or_13 (or_13_out, reset, start);
  Multiplexer #(.Bits(8)) multiplexer_3 (.sel(_30), .in_0(operand), .in_1(multiplexer_4_out), .out(multiplexer_3_out));
  Multiplexer #(.Bits(8)) multiplexer_4 (
    .sel(ENABLE_N), .in_0({4'b0000, operand[7:4]}), .in_1({4'b0000, operand[3:0]}), .out(multiplexer_4_out));
  or or_14 (ENABLE_LCD1, and_4_out, ENABLE_LCD2);
  Multiplexer #(.Bits(8)) multiplexer_5 (
    .sel(or_13_out), .in_0(multiplexer_2_out), .in_1({8{1'b0}}), .out(multiplexer_5_out));
  Comparator #(.Bits(8)) comparator_7 (.a(counter_2_out), .b(8'hf), .gt(done));  // open: eq, lt
  Multiplexer #(.Bits(8)) multiplexer_6 (
    .sel(rRAM_read), .in_0(counter_2_out), .in_1(multiplexer_3_out), .out(multiplexer_6_out));
  Register register_3 (.D(reset), .C(clk), .en(reset), .Q(register_3_q));
  and and_5 (and_5_out, _11, ~reset);  // And
  or or_15 (or_15_out, EQ, GT);
  Register #(.Bits(8), .isProgramCounter("true")) register_4 (
    .D(multiplexer_5_out), .C(clk), .en(ENABLE_PC), .Q(register_4_q));
  Counter #(.Bits(8)) counter_3 (.en(progLoad), .C(clk), .clr(reset), .out(counter_3_out));  // open: ovf
  Counter #(.Bits(8)) counter_4 (.en(progLoad), .C(clk), .clr(reset), .out(counter_4_out));  // open: ovf
  Multiplexer #(.Bits(8)) multiplexer_7 (
    .sel(ENABLE_LCD1), .in_0(rRAM_PC), .in_1(multiplexer_8_out), .out(multiplexer_7_out));
  Multiplexer #(.Bits(8)) multiplexer_8 (.sel(ENABLE_LCD2), .in_0(8'he), .in_1(8'hf), .out(multiplexer_8_out));
  or or_16 (LOAD_B, _2, _4);
  or or_17 (LOAD_C, _8, _7, _5);
  or or_18 (regC_set2, _8, _7);
  or or_19 (accA_set2, _6, _10);
  or or_20 (accA_set3, _3, _6, _10);
  and and_6 (and_6_out, _13, EQ);
  and and_7 (and_7_out, _14, GT);
  and and_8 (and_8_out, _15, LE);
  and and_9 (and_9_out, _16, or_15_out);
  or or_21 (or_21_out, _11, ENABLE_reset);
  Multiplexer #(.Bits(8)) multiplexer_9 (
    .sel(ENABLE_reset), .in_0(operand), .in_1(multiplexer_7_out), .out(multiplexer_9_out));
  Multiplexer #(.Bits(8)) multiplexer_10 (
    .sel(ENABLE_LCD2), .in_0(LCM[15:8]), .in_1(LCM[7:0]), .out(multiplexer_10_out));
  and and_10 (and_10_out, register_3_q, ~and_5_out);  // And
  Multiplexer #(.Bits(8)) multiplexer_11 (
    .sel(ENABLE_reset), .in_0(out_15), .in_1(multiplexer_12_out), .out(multiplexer_11_out));
  Multiplexer #(.Bits(8)) multiplexer_12 (
    .sel(ENABLE_LCD1), .in_0({8{1'b0}}), .in_1(multiplexer_10_out), .out(multiplexer_12_out));
  or or_22 (ENABLE_reset, and_10_out, _30);
  or or_23 (Jump_PC, _12, and_6_out, and_7_out, and_8_out, and_9_out);
  RAMDualAccess #(.AddrBits(8), .isProgramMemory("true"), .Bits(13)) pRAM (
    .str(progLoad), .C(clk), .ld(1'b1), .A1(counter_3_out), .Din1(progIN), .A2(register_4_q), .D1(out_12),
    .D2({out_18, operand}));
  RAMDualAccess #(.AddrBits(8), .Bits(8)) u_rRAM (
    .str(or_21_out), .C(clk), .ld(1'b1), .A1(multiplexer_9_out), .Din1(multiplexer_11_out),
    .A2(multiplexer_6_out), .D2(rRAM));  // open: D1
  RAMDualAccess #(.AddrBits(8), .isProgramMemory("true"), .Bits(13)) pRAM_copy (
    .str(progLoad), .C(clk), .ld(1'b1), .A1(counter_4_out), .Din1(progIN), .A2(operand), .D1(out_13),
    .D2({out_14, operand_copy}));
  Multiplexer #(.Bits(8)) multiplexer_13 (.sel(finalresult), .in_0({8{1'b0}}), .in_1(rRAM), .out(\output ));
  Add #(.Bits(8)) add_1 (.a(register_4_q), .b({8{1'b0}}), .c_i(1'b1), .s(add_1_s));  // open: c_o
  Seven_Seg_Hex seven_seg_hex_1 (.d(\output [7:4]), .dp(1'b0));
  Seven_Seg_Hex seven_seg_hex_2 (.d(\output [3:0]), .dp(1'b0));
  Register #(.Bits(8)) u_M (.D(rRAM), .C(clk), .en(ENABLE_M), .Q(MM));
  Register #(.Bits(8)) u_N (.D(rRAM), .C(clk), .en(ENABLE_N), .Q(NN));
  Multiplexer #(.Bits(8)) multiplexer_14 (.sel(_8), .in_0(M), .in_1(N), .out(multiplexer_14_out));
  Multiplexer #(.Bits(8)) multiplexer_15 (.sel(reset), .in_0(add_2_s), .in_1({8{1'b0}}), .out(multiplexer_15_out));
  Comparator #(.Bits(8)) comparator_8 (.a(GCD_PC), .b(8'h3), .gt(comparator_8_gt));  // open: eq, lt
  Comparator #(.Bits(8)) comparator_9 (.a(GCD_PC), .b(8'h3), .eq(comparator_9_eq));  // open: gt, lt
  Multiplexer #(.Bits(8)) multiplexer_16 (.sel(_10), .in_0(out_17), .in_1(rRAM), .out(multiplexer_16_out));
  and and_11 (and_11_out, comparator_8_gt, ~GCDbusy);  // And
  Multiplexer #(.Bits(8)) multiplexer_17 (
    .sel(accA_set2), .in_0(out_16), .in_1(multiplexer_16_out), .out(multiplexer_17_out));
  Multiplexer #(.Bits(8)) multiplexer_18 (
    .sel(regC_set2), .in_0(out_15), .in_1(multiplexer_14_out), .out(multiplexer_18_out));
  Register #(.Bits(8), .isProgramCounter("true")) register_5 (
    .D(multiplexer_15_out), .C(clk), .en(ENABLE_reset), .Q(rRAM_PC));
  Register #(.Bits(8), .isProgramCounter("true")) GCDpc (.D(add_3_s), .C(clk), .en(_30), .Q(GCD_PC));
  Register #(.Bits(8), .isProgramCounter("true")) LCMpc (.D(add_4_s), .C(clk), .en(and_11_out), .Q(LCM_PC));
  Multiplexer #(.Bits(8)) multiplexer_19 (.sel(GCDbusy), .in_0(MM), .in_1(register_6_q), .out(multiplexer_19_out));
  Multiplexer #(.Bits(8)) multiplexer_20 (.sel(GCDbusy), .in_0(NN), .in_1(register_7_q), .out(multiplexer_20_out));
  Register #(.Bits(8)) C (.D(multiplexer_18_out), .C(clk), .en(LOAD_C), .Q(out_17));
  Multiplexer #(.Bits(8)) multiplexer_21 (
    .sel(accA_set3), .in_0(ALU), .in_1(multiplexer_17_out), .out(multiplexer_21_out));
  Sub #(.Bits(8)) sub_1 (.a(multiplexer_19_out), .b(multiplexer_20_out), .c_i(1'b0), .s(sub_1_s));  // open: c_o
  Sub #(.Bits(8)) sub_2 (.a(multiplexer_20_out), .b(multiplexer_19_out), .c_i(1'b0), .s(sub_2_s));  // open: c_o
  Multiplexer #(.Bits(8)) multiplexer_22 (
    .sel(accA_set4), .in_0(operand_copy), .in_1(multiplexer_21_out), .out(multiplexer_22_out));
  Comparator #(.Bits(8)) comparator_10 (
    .a(multiplexer_19_out), .b(multiplexer_20_out), .gt(comparator_10_gt));  // open: eq, lt
  Multiplexer #(.Bits(8)) multiplexer_23 (.sel(_4), .in_0(operand), .in_1(out_15), .out(multiplexer_23_out));
  Multiplexer #(.Bits(8)) multiplexer_24 (
    .sel(accA_set5), .in_0(operand), .in_1(multiplexer_22_out), .out(multiplexer_24_out));
  Multiplexer #(.Bits(8)) multiplexer_25 (
    .sel(comparator_10_gt), .in_0(sub_2_s), .in_1(sub_1_s), .out(multiplexer_25_out));
  Multiplexer #(.Bits(8)) multiplexer_26 (
    .sel(comparator_10_gt), .in_0(multiplexer_19_out), .in_1(multiplexer_20_out), .out(multiplexer_26_out));
  Register #(.Bits(8)) B (.D(multiplexer_23_out), .C(clk), .en(LOAD_B), .Q(out_16));
  Register #(.Bits(8)) A (.D(multiplexer_24_out), .C(clk), .en(LOAD_A), .Q(out_15));
  Add #(.Bits(8)) add_2 (.a(rRAM_PC), .b({8{1'b0}}), .c_i(1'b1), .s(add_2_s));  // open: c_o
  Add #(.Bits(8)) add_3 (.a(GCD_PC), .b({8{1'b0}}), .c_i(1'b1), .s(add_3_s));  // open: c_o
  Add #(.Bits(8)) add_4 (.a(LCM_PC), .b({8{1'b0}}), .c_i(1'b1), .s(add_4_s));  // open: c_o
  Register #(.Bits(8)) register_6 (.D(multiplexer_25_out), .C(clk), .en(and_12_out), .Q(register_6_q));
  Register #(.Bits(8)) register_7 (.D(multiplexer_26_out), .C(clk), .en(and_12_out), .Q(register_7_q));
  and and_12 (and_12_out, or_24_out, or_27_out);
  or or_24 (or_24_out, comparator_9_eq, GCDbusy);
  Comparator #(.Signed("true"), .Bits(8)) comparator_11 (.a(out_15), .b(out_16), .gt(gt_t), .eq(eq_t), .lt(le_t));
  assign \and  = out_15 & out_16;  // And and_13, 8 bits wide
  assign \or  = out_15 | out_16;  // Or or_25, 8 bits wide
  assign \xor  = out_15 ^ out_16;  // XOr xor_1, 8 bits wide
  Comparator #(.Bits(8)) comparator_12 (
    .a(register_6_q), .b(register_7_q), .gt(comparator_12_gt), .eq(comparator_12_eq));  // open: lt
  Add #(.Bits(8)) add_5 (.a(out_15), .b(out_16), .c_i(1'b0), .s(add));  // open: c_o
  Sub #(.Bits(8)) sub_3 (.a(out_15), .b(out_16), .c_i(1'b0), .s(sub));  // open: c_o
  Div #(.Bits(8)) div_1 (.a(out_15), .b(out_16), .q(divide), .r(mod));
  assign \not  = ~out_15;  // Not not_1, 8 bits wide
  BarrelShifter #(.Bits(8)) barrelshifter_1 (.in(out_15), .shift(out_16[3:0]), .out(shift));
  Mul #(.Bits(4)) mul_1 (.a(out_15[3:0]), .b(out_16[3:0]), .mul(mul));
  ROM #(.AddrBits(6), .Bits(8)) rom_1 (.A({out_15[2:0], out_16[2:0]}), .sel(1'b1), .D(power));
  and and_14 (isprime, _29, prime);
  Multiplexer #(.Bits(8)) multiplexer_27 (
    .sel(and_15_out), .in_0(register_6_q), .in_1(register_7_q), .out(multiplexer_27_out));
  Comparator #(.Bits(8)) comparator_13 (.a(register_7_q), .b({8{1'b0}}), .eq(comparator_13_eq));  // open: gt, lt
  and and_15 (and_15_out, comparator_12_eq, comparator_12_gt);
  not not_2 (GCDbusy, comparator_12_eq);
  Multiplexer multiplexer_28 (.sel(_29), .in_0(eq_t), .in_1(isprime), .out(multiplexer_28_out));
  or or_26 (or_26_out, _23, _29);
  or or_27 (or_27_out, GCDbusy, comparator_13_eq);
  Register register_8 (.D(gt_t), .C(clk), .en(_23), .Q(GT));
  Register register_9 (.D(multiplexer_28_out), .C(clk), .en(or_26_out), .Q(EQ));
  Register register_10 (.D(le_t), .C(clk), .en(_23), .Q(LE));
  Mul #(.Bits(8)) mul_2 (.a(NN), .b(MM), .mul(mul_2_mul));
  Multiplexer #(.Bits(8)) multiplexer_29 (.sel(GCDbusy), .in_0(multiplexer_27_out), .in_1({8{1'b0}}), .out(GCD));
  Div #(.Bits(16)) div_2 (.a(mul_2_mul), .b({{8{1'b0}}, GCD}), .q(LCM));  // open: r
  Multiplexer #(.Selector_Bits(4), .Bits(8)) multiplexer_30 (
    .sel(out_18[3:0]), .in_0({8{1'b0}}), .in_1(add), .in_2(sub), .in_3(mul), .in_4(divide), .in_5(mod),
    .in_6(power), .in_7({8{1'b0}}), .in_8(\not ), .in_9(\and ), .in_10(\or ), .in_11(\xor ), .in_12(shift),
    .in_13({8{1'b0}}), .in_14({8{1'b0}}), .in_15({8{1'b0}}), .out(ALU));

  // Other names for the same wires on the sheet: Oppcode[4:0] = out_18; _31 = valid; A[7:0] = out_15; accA_set1 = _10;
  //   accB_set = _4; B[7:0] = out_16; C[7:0] = out_17; clock = clk; GCD_busy = GCDbusy; GCD_read1 = _30;
  //   GCD_read2 = ENABLE_N; LOAD_cmp = _23; regC_set1 = _8; rRAM_load = _11

  // Notes on the sheet:
  //   control unit
  //   ..
  //   ALU+
  //   Acc
  //   ALU
  //   contents of rom_1 (hex, n*v repeats v):
  //   8*0,9*1,2,4,8,10,20,40,80,1,3,9,1b,51,f3,2d9,88b,1,4,10,40,100
  //   ,400,1000,4000,1,5,19,7d,271,c35,3d09,1312d,1,6,24,d8,510,1e60
  //   ,b640,44580,1,7,31,157,961,41a7,1cb91,c90f7
endmodule

/* Test case 01_P01T2:
M N progIN reset progLoad start result clk valid done output
0 0 0 0 0 0 0 0 x x x
0 0 0 0 0 0 0 1 x x x
0 0 0 1 0 0 0 0 x x x
0 0 0 1 0 0 0 1 0 0 0
0 0 0 0 0 0 0 0 0 0 0
0 0 0 0 0 0 0 1 0 0 0
0 0 0 0 0 0 0 0 0 0 0
0 0 0 0 0 0 0 1 0 0 0
0 0 0 0 0 0 0 0 0 0 0
0 0 0 0 0 0 0 1 0 0 0
0 0 0 0 0 0 0 0 0 0 0
0 0 0 0 0 0 0 1 0 0 0
0 0 0 0 0 0 0 0 0 0 0
0 0 0 0 0 0 0 1 0 0 0
0 0 0 0 0 0 0 0 0 0 0
0 0 0 0 0 0 0 1 0 0 0
0 0 0 0 0 0 0 0 0 0 0
0 0 0 0 0 0 0 1 0 0 0
0 0 0 0 0 0 0 0 0 0 0
0 0 0 0 0 0 0 1 0 0 0
0 0 0 0 0 0 0 0 0 0 0
0 0 0 0 0 0 0 1 0 0 0
0 0 0 0 0 0 0 0 0 0 0
0 0 0 0 0 0 0 1 0 0 0
0 0 0 0 0 0 0 0 0 0 0
0 0 0 0 0 0 0 1 0 0 0
0 0 0 0 0 0 0 0 0 0 0
0 0 0 0 0 0 0 1 0 0 0
0 0 0 0 0 0 0 0 0 0 0
0 0 0 0 0 0 0 1 0 0 0
0 0 0 0 0 0 0 0 0 0 0
0 0 0 0 0 0 0 1 0 0 0
0 0 0 0 0 0 0 0 0 0 0
0 0 0 0 0 0 0 1 0 0 0
0 0 0 0 0 0 0 0 0 0 0
0 0 0 0 0 0 0 1 0 0 0
0 0 0 0 0 0 0 0 0 0 0
0 0 0 0 0 0 0 1 0 0 0
0 0 0 0 0 0 0 0 0 0 0
0 0 0 0 0 0 0 1 0 0 0
0 0 0 0 0 0 0 0 0 0 0
0 0 0 0 0 0 0 1 0 0 0
0 0 271 0 1 0 0 0 0 0 0
0 0 271 0 1 0 0 1 0 0 0
0 0 565 0 1 0 0 0 0 0 0
0 0 565 0 1 0 0 1 0 0 0
0 0 4352 0 1 0 0 0 0 0 0
0 0 4352 0 1 0 0 1 0 0 0
0 0 2819 0 1 0 0 0 0 0 0
0 0 2819 0 1 0 0 1 0 0 0
0 0 7936 0 1 0 0 0 0 0 0
0 0 7936 0 1 0 0 1 0 0 0
0 0 0 0 0 1 0 0 0 0 0
0 0 0 0 0 1 0 1 0 0 0
0 0 0 0 0 0 0 0 x 0 0
0 0 0 0 0 0 0 1 x 0 0
0 0 0 0 0 0 0 0 x 0 0
0 0 0 0 0 0 0 1 x 0 0
0 0 0 0 0 0 0 0 x 0 0
0 0 0 0 0 0 0 1 x 0 0
0 0 0 0 0 0 0 0 x 0 0
0 0 0 0 0 0 0 1 x 0 0
0 0 0 0 0 0 0 0 x 0 0
0 0 0 0 0 0 0 1 x 0 0
0 0 0 0 0 0 0 0 x 0 0
0 0 0 0 0 0 0 1 x 0 0
0 0 0 0 0 0 0 0 x 0 0
0 0 0 0 0 0 0 1 x 0 0
0 0 0 0 0 0 0 0 x 0 0
0 0 0 0 0 0 0 1 x 0 0
0 0 0 0 0 0 0 0 x 0 0
0 0 0 0 0 0 0 1 x 0 0
0 0 0 0 0 0 0 0 x 0 0
0 0 0 0 0 0 0 1 x 0 0
0 0 0 0 0 0 0 0 x 0 0
0 0 0 0 0 0 0 1 x 0 0
0 0 0 0 0 0 0 0 x 0 0
0 0 0 0 0 0 0 1 x 0 0
0 0 0 0 0 0 0 0 x 0 0
0 0 0 0 0 0 0 1 x 0 0
0 0 0 0 0 0 0 0 x 0 0
0 0 0 0 0 0 0 1 x 0 0
0 0 0 0 0 0 0 0 x 0 0
0 0 0 0 0 0 0 1 x 0 0
0 0 0 0 0 0 0 0 x 0 0
0 0 0 0 0 0 0 1 x 0 0
0 0 0 0 0 0 0 0 x 0 0
0 0 0 0 0 0 0 1 x 0 0
0 0 0 0 0 0 0 0 x 0 0
0 0 0 0 0 0 0 1 x 0 0
0 0 0 0 0 0 0 0 x 0 0
0 0 0 0 0 0 0 1 x 0 0
0 0 0 0 0 0 0 0 x 0 0
0 0 0 0 0 0 0 1 x 0 0
0 0 0 0 0 0 0 0 x 0 0
0 0 0 0 0 0 0 1 x 0 0
0 0 0 0 0 0 0 0 x 0 0
0 0 0 0 0 0 0 1 x 0 0
0 0 0 0 0 0 0 0 x 0 0
0 0 0 0 0 0 0 1 x 0 0
0 0 0 0 0 0 0 0 x 0 0
0 0 0 0 0 0 0 1 x 0 0
0 0 0 0 0 0 0 0 x 0 0
0 0 0 0 0 0 0 1 x 0 0
0 0 0 0 0 0 0 0 x 0 0
0 0 0 0 0 0 0 1 1 0 0
0 0 0 0 0 0 1 0 1 0 0
0 0 0 0 0 0 1 1 1 0 0
0 0 0 0 0 0 0 0 1 0 0
0 0 0 0 0 0 0 1 1 0 0
0 0 0 0 0 0 0 0 1 0 0
0 0 0 0 0 0 0 1 1 0 0
0 0 0 0 0 0 0 0 1 0 0
0 0 0 0 0 0 0 1 1 0 68
0 0 0 0 0 0 0 0 1 0 68
0 0 0 0 0 0 0 1 1 0 0
0 0 0 0 0 0 0 0 1 0 0
0 0 0 0 0 0 0 1 1 0 0
0 0 0 0 0 0 0 0 1 0 0
0 0 0 0 0 0 0 1 1 0 0
0 0 0 0 0 0 0 0 1 0 0
0 0 0 0 0 0 0 1 1 0 0
0 0 0 0 0 0 0 0 1 0 0
0 0 0 0 0 0 0 1 1 0 0
0 0 0 0 0 0 0 0 1 0 0
0 0 0 0 0 0 0 1 1 0 0
0 0 0 0 0 0 0 0 1 0 0
0 0 0 0 0 0 0 1 1 0 0
0 0 0 0 0 0 0 0 1 0 0
0 0 0 0 0 0 0 1 1 0 0
0 0 0 0 0 0 0 0 1 0 0
0 0 0 0 0 0 0 1 1 0 0
0 0 0 0 0 0 0 0 1 0 0
0 0 0 0 0 0 0 1 1 0 0
0 0 0 0 0 0 0 0 1 0 0
0 0 0 0 0 0 0 1 1 0 0
0 0 0 0 0 0 0 0 1 0 0
0 0 0 0 0 0 0 1 1 0 0
0 0 0 0 0 0 0 0 1 0 0
0 0 0 0 0 0 0 1 1 1 0
0 0 0 0 0 0 0 0 1 1 0
0 0 0 0 0 0 0 1 1 1 0
0 0 0 0 0 0 0 0 1 1 0
*/

/* Test case 05_P04T1:
M N progIN reset progLoad start result clk valid done output
0 0 0 0 0 0 0 0 x x x
0 0 0 0 0 0 0 1 x x x
0 0 0 1 0 0 0 0 x x x
0 0 0 1 0 0 0 1 0 0 x
0 0 0 0 0 0 0 0 0 0 x
0 0 0 0 0 0 0 1 0 0 x
0 0 0 0 0 0 0 0 0 0 x
0 0 0 0 0 0 0 1 0 0 x
0 0 0 0 0 0 0 0 0 0 x
0 0 0 0 0 0 0 1 0 0 x
0 0 0 0 0 0 0 0 0 0 x
0 0 0 0 0 0 0 1 0 0 x
0 0 0 0 0 0 0 0 0 0 x
0 0 0 0 0 0 0 1 0 0 x
0 0 0 0 0 0 0 0 0 0 x
0 0 0 0 0 0 0 1 0 0 x
0 0 0 0 0 0 0 0 0 0 x
0 0 0 0 0 0 0 1 0 0 x
0 0 0 0 0 0 0 0 0 0 x
0 0 0 0 0 0 0 1 0 0 x
0 0 0 0 0 0 0 0 0 0 x
0 0 0 0 0 0 0 1 0 0 x
0 0 0 0 0 0 0 0 0 0 x
0 0 0 0 0 0 0 1 0 0 x
0 0 0 0 0 0 0 0 0 0 x
0 0 0 0 0 0 0 1 0 0 x
0 0 0 0 0 0 0 0 0 0 x
0 0 0 0 0 0 0 1 0 0 x
0 0 0 0 0 0 0 0 0 0 x
0 0 0 0 0 0 0 1 0 0 x
0 0 0 0 0 0 0 0 0 0 x
0 0 0 0 0 0 0 1 0 0 x
0 0 0 0 0 0 0 0 0 0 x
0 0 0 0 0 0 0 1 0 0 x
0 0 0 0 0 0 0 0 0 0 x
0 0 0 0 0 0 0 1 0 0 x
0 0 0 0 0 0 0 0 0 0 x
0 0 0 0 0 0 0 1 0 0 x
0 0 0 0 0 0 0 0 0 0 x
0 0 0 0 0 0 0 1 0 0 x
0 0 0 0 0 0 0 0 0 0 x
0 0 0 0 0 0 0 1 0 0 x
0 0 0 0 0 0 0 0 0 0 x
0 0 0 0 0 0 0 1 0 0 x
0 0 271 0 1 0 0 0 0 0 x
0 0 271 0 1 0 0 1 0 0 x
0 0 7424 0 1 0 0 0 0 0 x
0 0 7424 0 1 0 0 1 0 0 x
0 0 3328 0 1 0 0 0 0 0 x
0 0 3328 0 1 0 0 1 0 0 x
0 0 257 0 1 0 0 0 0 0 x
0 0 257 0 1 0 0 1 0 0 x
0 0 3331 0 1 0 0 0 0 0 x
0 0 3331 0 1 0 0 1 0 0 x
0 0 455 0 1 0 0 0 0 0 x
0 0 455 0 1 0 0 1 0 0 x
0 0 7424 0 1 0 0 0 0 0 x
0 0 7424 0 1 0 0 1 0 0 x
0 0 3337 0 1 0 0 0 0 0 x
0 0 3337 0 1 0 0 1 0 0 x
0 0 2818 0 1 0 0 0 0 0 x
0 0 2818 0 1 0 0 1 0 0 x
0 0 2819 0 1 0 0 0 0 0 x
0 0 2819 0 1 0 0 1 0 0 x
0 0 7936 0 1 0 0 0 0 0 x
0 0 7936 0 1 0 0 1 0 0 x
0 0 0 0 0 0 0 0 0 0 x
0 0 0 0 0 0 0 1 0 0 x
0 0 0 0 0 0 0 0 0 0 x
0 0 0 0 0 0 0 1 0 0 x
0 0 0 0 0 0 0 0 0 0 x
0 0 0 0 0 0 0 1 0 0 x
0 0 0 0 0 1 0 0 0 0 x
0 0 0 0 0 1 0 1 0 0 x
0 0 0 0 0 0 0 0 x 0 x
0 0 0 0 0 0 0 1 x 0 x
0 0 0 0 0 0 0 0 x 0 x
0 0 0 0 0 0 0 1 x 0 x
0 0 0 0 0 0 0 0 x 0 x
0 0 0 0 0 0 0 1 x 0 x
0 0 0 0 0 0 0 0 x 0 x
0 0 0 0 0 0 0 1 x 0 x
0 0 0 0 0 0 0 0 x 0 x
0 0 0 0 0 0 0 1 x 0 x
0 0 0 0 0 0 0 0 x 0 x
0 0 0 0 0 0 0 1 x 0 x
0 0 0 0 0 0 0 0 x 0 x
0 0 0 0 0 0 0 1 x 0 x
0 0 0 0 0 0 0 0 x 0 x
0 0 0 0 0 0 0 1 x 0 x
0 0 0 0 0 0 0 0 x 0 x
0 0 0 0 0 0 0 1 x 0 x
0 0 0 0 0 0 0 0 x 0 x
0 0 0 0 0 0 0 1 x 0 x
0 0 0 0 0 0 0 0 x 0 x
0 0 0 0 0 0 0 1 x 0 x
0 0 0 0 0 0 0 0 x 0 x
0 0 0 0 0 0 0 1 x 0 x
0 0 0 0 0 0 0 0 x 0 x
0 0 0 0 0 0 0 1 x 0 x
0 0 0 0 0 0 0 0 x 0 x
0 0 0 0 0 0 0 1 x 0 x
0 0 0 0 0 0 0 0 x 0 x
0 0 0 0 0 0 0 1 x 0 x
0 0 0 0 0 0 0 0 x 0 x
0 0 0 0 0 0 0 1 x 0 x
0 0 0 0 0 0 0 0 x 0 x
0 0 0 0 0 0 0 1 x 0 x
0 0 0 0 0 0 0 0 x 0 x
0 0 0 0 0 0 0 1 x 0 x
0 0 0 0 0 0 0 0 x 0 x
0 0 0 0 0 0 0 1 x 0 x
0 0 0 0 0 0 0 0 x 0 x
0 0 0 0 0 0 0 1 x 0 x
0 0 0 0 0 0 0 0 x 0 x
0 0 0 0 0 0 0 1 x 0 x
0 0 0 0 0 0 0 0 x 0 x
0 0 0 0 0 0 0 1 x 0 x
0 0 0 0 0 0 0 0 x 0 x
0 0 0 0 0 0 0 1 x 0 x
0 0 0 0 0 0 0 0 x 0 x
0 0 0 0 0 0 0 1 x 0 x
0 0 0 0 0 0 0 0 x 0 x
0 0 0 0 0 0 0 1 x 0 x
0 0 0 0 0 0 0 0 x 0 x
0 0 0 0 0 0 0 1 x 0 x
0 0 0 0 0 0 0 0 x 0 x
0 0 0 0 0 0 0 1 x 0 x
0 0 0 0 0 0 0 0 x 0 x
0 0 0 0 0 0 0 1 x 0 x
0 0 0 0 0 0 0 0 x 0 x
0 0 0 0 0 0 0 1 x 0 x
0 0 0 0 0 0 0 0 x 0 x
0 0 0 0 0 0 0 1 x 0 x
0 0 0 0 0 0 0 0 x 0 x
0 0 0 0 0 0 0 1 x 0 x
0 0 0 0 0 0 0 0 x 0 x
0 0 0 0 0 0 0 1 x 0 x
0 0 0 0 0 0 0 0 x 0 x
0 0 0 0 0 0 0 1 x 0 x
0 0 0 0 0 0 0 0 x 0 x
0 0 0 0 0 0 0 1 x 0 x
0 0 0 0 0 0 0 0 x 0 x
0 0 0 0 0 0 0 1 x 0 x
0 0 0 0 0 0 0 0 x 0 x
0 0 0 0 0 0 0 1 x 0 x
0 0 0 0 0 0 0 0 x 0 x
0 0 0 0 0 0 0 1 x 0 x
0 0 0 0 0 0 0 0 x 0 x
0 0 0 0 0 0 0 1 x 0 x
0 0 0 0 0 0 0 0 x 0 x
0 0 0 0 0 0 0 1 x 0 x
0 0 0 0 0 0 0 0 x 0 x
0 0 0 0 0 0 0 1 x 0 x
0 0 0 0 0 0 0 0 x 0 x
0 0 0 0 0 0 0 1 x 0 x
0 0 0 0 0 0 0 0 x 0 x
0 0 0 0 0 0 0 1 x 0 x
0 0 0 0 0 0 0 0 x 0 x
0 0 0 0 0 0 0 1 x 0 x
0 0 0 0 0 0 0 0 x 0 x
0 0 0 0 0 0 0 1 x 0 x
0 0 0 0 0 0 0 0 x 0 x
0 0 0 0 0 0 0 1 x 0 x
0 0 0 0 0 0 0 0 x 0 x
0 0 0 0 0 0 0 1 x 0 x
0 0 0 0 0 0 0 0 x 0 x
0 0 0 0 0 0 0 1 x 0 x
0 0 0 0 0 0 0 0 x 0 x
0 0 0 0 0 0 0 1 x 0 x
0 0 0 0 0 0 0 0 x 0 x
0 0 0 0 0 0 0 1 x 0 x
0 0 0 0 0 0 0 0 x 0 x
0 0 0 0 0 0 0 1 x 0 x
0 0 0 0 0 0 0 0 x 0 x
0 0 0 0 0 0 0 1 x 0 x
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*/

/* Test case t9:
M	N	progIN	reset	progLoad	start	result	clk	valid	done	output
0	0	0	0	0	0	0	0	x	x	x
0	0	0	0	0	0	0	1	x	x	x
0	0	0	1	0	0	0	0	x	x	x
0	0	0	1	0	0	0	1	0	0	0
0	0	0	0	0	0	0	0	0	0	0
0	0	0	0	0	0	0	1	0	0	0
0	0	0	0	0	0	0	0	0	0	0
0	0	0	0	0	0	0	1	0	0	0
0	0	0	0	0	0	0	0	0	0	0
0	0	0	0	0	0	0	1	0	0	0
0	0	0	0	0	0	0	0	0	0	0
0	0	0	0	0	0	0	1	0	0	0
0	0	0	0	0	0	0	0	0	0	0
0	0	0	0	0	0	0	1	0	0	0
0	0	0	0	0	0	0	0	0	0	0
0	0	0	0	0	0	0	1	0	0	0
0	0	0	0	0	0	0	0	0	0	0
0	0	0	0	0	0	0	1	0	0	0
0	0	0	0	0	0	0	0	0	0	0
0	0	0	0	0	0	0	1	0	0	0
0	0	0	0	0	0	0	0	0	0	0
0	0	0	0	0	0	0	1	0	0	0
0	0	0	0	0	0	0	0	0	0	0
0	0	0	0	0	0	0	1	0	0	0
0	0	0	0	0	0	0	0	0	0	0
0	0	0	0	0	0	0	1	0	0	0
0	0	0	0	0	0	0	0	0	0	0
0	0	0	0	0	0	0	1	0	0	0
0	0	0	0	0	0	0	0	0	0	0
0	0	0	0	0	0	0	1	0	0	0
0	0	0	0	0	0	0	0	0	0	0
0	0	0	0	0	0	0	1	0	0	0
0	0	0	0	0	0	0	0	0	0	0
0	0	0	0	0	0	0	1	0	0	0
0	0	0	0	0	0	0	0	0	0	0
0	0	0	0	0	0	0	1	0	0	0
0	0	0	0	0	0	0	0	0	0	0
0	0	0	0	0	0	0	1	0	0	0
0	0	0	0	0	0	0	0	0	0	0
0	0	0	0	0	0	0	1	0	0	0
0	0	0	0	0	0	0	0	0	0	0
0	0	0	0	0	0	0	1	0	0	0
0	0	271	0	1	0	0	0	0	0	0
0	0	271	0	1	0	0	1	0	0	0
0	0	566	0	1	0	0	0	0	0	0
0	0	566	0	1	0	0	1	0	0	0
0	0	5888	0	1	0	0	0	0	0	0
0	0	5888	0	1	0	0	1	0	0	0
0	0	3599	0	1	0	0	0	0	0	0
0	0	3599	0	1	0	0	1	0	0	0
0	0	4110	0	1	0	0	0	0	0	0
0	0	4110	0	1	0	0	1	0	0	0
0	0	3856	0	1	0	0	0	0	0	0
0	0	3856	0	1	0	0	1	0	0	0
0	0	0	0	1	0	0	0	0	0	0
0	0	0	0	1	0	0	1	0	0	0
0	0	0	0	1	0	0	0	0	0	0
0	0	0	0	1	0	0	1	0	0	0
0	0	0	0	1	0	0	0	0	0	0
0	0	0	0	1	0	0	1	0	0	0
0	0	0	0	1	0	0	0	0	0	0
0	0	0	0	1	0	0	1	0	0	0
0	0	0	0	1	0	0	0	0	0	0
0	0	0	0	1	0	0	1	0	0	0
0	0	0	0	1	0	0	0	0	0	0
0	0	0	0	1	0	0	1	0	0	0
0	0	0	0	1	0	0	0	0	0	0
0	0	0	0	1	0	0	1	0	0	0
0	0	0	0	1	0	0	0	0	0	0
0	0	0	0	1	0	0	1	0	0	0
0	0	0	0	1	0	0	0	0	0	0
0	0	0	0	1	0	0	1	0	0	0
0	0	0	0	1	0	0	0	0	0	0
0	0	0	0	1	0	0	1	0	0	0
0	0	4352	0	1	0	0	0	0	0	0
0	0	4352	0	1	0	0	1	0	0	0
0	0	2819	0	1	0	0	0	0	0	0
0	0	2819	0	1	0	0	1	0	0	0
0	0	7936	0	1	0	0	0	0	0	0
0	0	7936	0	1	0	0	1	0	0	0
0	0	0	0	1	0	0	0	0	0	0
0	0	0	0	1	0	0	1	0	0	0
0	0	0	0	0	0	0	0	0	0	0
0	0	0	0	0	0	0	1	0	0	0
0	0	0	0	0	0	0	0	0	0	0
0	0	0	0	0	0	0	1	0	0	0
0	0	0	0	0	0	0	0	0	0	0
0	0	0	0	0	0	0	1	0	0	0
0	0	0	0	0	1	0	0	0	0	0
0	0	0	0	0	1	0	1	0	0	0
0	0	0	0	0	0	0	0	x	0	0
0	0	0	0	0	0	0	1	x	0	0
0	0	0	0	0	0	0	0	x	0	0
0	0	0	0	0	0	0	1	x	0	0
0	0	0	0	0	0	0	0	x	0	0
0	0	0	0	0	0	0	1	x	0	0
0	0	0	0	0	0	0	0	x	0	0
0	0	0	0	0	0	0	1	x	0	0
0	0	0	0	0	0	0	0	x	0	0
0	0	0	0	0	0	0	1	x	0	0
0	0	0	0	0	0	0	0	x	0	0
0	0	0	0	0	0	0	1	x	0	0
0	0	0	0	0	0	0	0	x	0	0
0	0	0	0	0	0	0	1	x	0	0
0	0	0	0	0	0	0	0	x	0	0
0	0	0	0	0	0	0	1	x	0	0
0	0	0	0	0	0	0	0	x	0	0
0	0	0	0	0	0	0	1	x	0	0
0	0	0	0	0	0	0	0	x	0	0
0	0	0	0	0	0	0	1	x	0	0
0	0	0	0	0	0	0	0	x	0	0
0	0	0	0	0	0	0	1	x	0	0
0	0	0	0	0	0	0	0	x	0	0
0	0	0	0	0	0	0	1	x	0	0
0	0	0	0	0	0	0	0	x	0	0
0	0	0	0	0	0	0	1	x	0	0
0	0	0	0	0	0	0	0	x	0	0
0	0	0	0	0	0	0	1	x	0	0
0	0	0	0	0	0	0	0	x	0	0
0	0	0	0	0	0	0	1	x	0	0
0	0	0	0	0	0	0	0	x	0	0
0	0	0	0	0	0	0	1	x	0	0
0	0	0	0	0	0	0	0	x	0	0
0	0	0	0	0	0	0	1	x	0	0
0	0	0	0	0	0	0	0	x	0	0
0	0	0	0	0	0	0	1	x	0	0
0	0	0	0	0	0	0	0	x	0	0
0	0	0	0	0	0	0	1	x	0	0
0	0	0	0	0	0	0	0	x	0	0
0	0	0	0	0	0	0	1	x	0	0
0	0	0	0	0	0	0	0	x	0	0
0	0	0	0	0	0	0	1	x	0	0
0	0	0	0	0	0	0	0	x	0	0
0	0	0	0	0	0	0	1	x	0	0
0	0	0	0	0	0	0	0	x	0	0
0	0	0	0	0	0	0	1	x	0	0
0	0	0	0	0	0	0	0	x	0	0
0	0	0	0	0	0	0	1	x	0	0
0	0	0	0	0	0	0	0	x	0	0
0	0	0	0	0	0	0	1	x	0	0
0	0	0	0	0	0	0	0	x	0	0
0	0	0	0	0	0	0	1	1	0	0
0	0	0	0	0	0	1	0	1	0	0
0	0	0	0	0	0	1	1	1	0	0
0	0	0	0	0	0	0	0	1	0	0
0	0	0	0	0	0	0	1	1	0	0
0	0	0	0	0	0	0	0	1	0	0
0	0	0	0	0	0	0	1	1	0	0
0	0	0	0	0	0	0	0	1	0	0
0	0	0	0	0	0	0	1	1	0	69
0	0	0	0	0	0	0	0	1	0	69
0	0	0	0	0	0	0	1	1	0	0
0	0	0	0	0	0	0	0	1	0	0
0	0	0	0	0	0	0	1	1	0	0
0	0	0	0	0	0	0	0	1	0	0
0	0	0	0	0	0	0	1	1	0	0
0	0	0	0	0	0	0	0	1	0	0
0	0	0	0	0	0	0	1	1	0	0
0	0	0	0	0	0	0	0	1	0	0
0	0	0	0	0	0	0	1	1	0	0
0	0	0	0	0	0	0	0	1	0	0
0	0	0	0	0	0	0	1	1	0	0
0	0	0	0	0	0	0	0	1	0	0
0	0	0	0	0	0	0	1	1	0	0
0	0	0	0	0	0	0	0	1	0	0
0	0	0	0	0	0	0	1	1	0	0
0	0	0	0	0	0	0	0	1	0	0
0	0	0	0	0	0	0	1	1	0	0
0	0	0	0	0	0	0	0	1	0	0
0	0	0	0	0	0	0	1	1	0	0
0	0	0	0	0	0	0	0	1	0	0
0	0	0	0	0	0	0	1	1	0	0
0	0	0	0	0	0	0	0	1	0	0
0	0	0	0	0	0	0	1	1	0	0
0	0	0	0	0	0	0	0	1	0	0
0	0	0	0	0	0	0	1	1	1	0
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*/

/* Test case 02_P01T3:
M N progIN reset progLoad start result clk valid done output
0 0 0 0 0 0 0 0 x x x
0 0 0 0 0 0 0 1 x x x
0 0 0 1 0 0 0 0 x x x
0 0 0 1 0 0 0 1 0 0 0
0 0 0 0 0 0 0 0 0 0 0
0 0 0 0 0 0 0 1 0 0 0
0 0 0 0 0 0 0 0 0 0 0
0 0 0 0 0 0 0 1 0 0 0
0 0 0 0 0 0 0 0 0 0 0
0 0 0 0 0 0 0 1 0 0 0
0 0 0 0 0 0 0 0 0 0 0
0 0 0 0 0 0 0 1 0 0 0
0 0 0 0 0 0 0 0 0 0 0
0 0 0 0 0 0 0 1 0 0 0
0 0 0 0 0 0 0 0 0 0 0
0 0 0 0 0 0 0 1 0 0 0
0 0 0 0 0 0 0 0 0 0 0
0 0 0 0 0 0 0 1 0 0 0
0 0 0 0 0 0 0 0 0 0 0
0 0 0 0 0 0 0 1 0 0 0
0 0 0 0 0 0 0 0 0 0 0
0 0 0 0 0 0 0 1 0 0 0
0 0 0 0 0 0 0 0 0 0 0
0 0 0 0 0 0 0 1 0 0 0
0 0 0 0 0 0 0 0 0 0 0
0 0 0 0 0 0 0 1 0 0 0
0 0 0 0 0 0 0 0 0 0 0
0 0 0 0 0 0 0 1 0 0 0
0 0 0 0 0 0 0 0 0 0 0
0 0 0 0 0 0 0 1 0 0 0
0 0 0 0 0 0 0 0 0 0 0
0 0 0 0 0 0 0 1 0 0 0
0 0 0 0 0 0 0 0 0 0 0
0 0 0 0 0 0 0 1 0 0 0
0 0 0 0 0 0 0 0 0 0 0
0 0 0 0 0 0 0 1 0 0 0
0 0 0 0 0 0 0 0 0 0 0
0 0 0 0 0 0 0 1 0 0 0
0 0 0 0 0 0 0 0 0 0 0
0 0 0 0 0 0 0 1 0 0 0
0 0 0 0 0 0 0 0 0 0 0
0 0 0 0 0 0 0 1 0 0 0
0 0 271 0 1 0 0 0 0 0 0
0 0 271 0 1 0 0 1 0 0 0
0 0 565 0 1 0 0 0 0 0 0
0 0 565 0 1 0 0 1 0 0 0
0 0 4352 0 1 0 0 0 0 0 0
0 0 4352 0 1 0 0 1 0 0 0
0 0 2819 0 1 0 0 0 0 0 0
0 0 2819 0 1 0 0 1 0 0 0
0 0 7936 0 1 0 0 0 0 0 0
0 0 7936 0 1 0 0 1 0 0 0
0 0 0 0 0 1 0 0 0 0 0
0 0 0 0 0 1 0 1 0 0 0
0 0 0 0 0 0 0 0 x 0 0
0 0 0 0 0 0 0 1 x 0 0
0 0 0 0 0 0 0 0 x 0 0
0 0 0 0 0 0 0 1 x 0 0
0 0 0 0 0 0 0 0 x 0 0
0 0 0 0 0 0 0 1 x 0 0
0 0 0 0 0 0 0 0 x 0 0
0 0 0 0 0 0 0 1 x 0 0
0 0 0 0 0 0 0 0 x 0 0
0 0 0 0 0 0 0 1 x 0 0
0 0 0 0 0 0 0 0 x 0 0
0 0 0 0 0 0 0 1 x 0 0
0 0 0 0 0 0 0 0 x 0 0
0 0 0 0 0 0 0 1 x 0 0
0 0 0 0 0 0 0 0 x 0 0
0 0 0 0 0 0 0 1 x 0 0
0 0 0 0 0 0 0 0 x 0 0
0 0 0 0 0 0 0 1 x 0 0
0 0 0 0 0 0 0 0 x 0 0
0 0 0 0 0 0 0 1 x 0 0
0 0 0 0 0 0 0 0 x 0 0
0 0 0 0 0 0 0 1 x 0 0
0 0 0 0 0 0 0 0 x 0 0
0 0 0 0 0 0 0 1 x 0 0
0 0 0 0 0 0 0 0 x 0 0
0 0 0 0 0 0 0 1 x 0 0
0 0 0 0 0 0 0 0 x 0 0
0 0 0 0 0 0 0 1 x 0 0
0 0 0 0 0 0 0 0 x 0 0
0 0 0 0 0 0 0 1 x 0 0
0 0 0 0 0 0 0 0 x 0 0
0 0 0 0 0 0 0 1 x 0 0
0 0 0 0 0 0 0 0 x 0 0
0 0 0 0 0 0 0 1 x 0 0
0 0 0 0 0 0 0 0 x 0 0
0 0 0 0 0 0 0 1 x 0 0
0 0 0 0 0 0 0 0 x 0 0
0 0 0 0 0 0 0 1 x 0 0
0 0 0 0 0 0 0 0 x 0 0
0 0 0 0 0 0 0 1 x 0 0
0 0 0 0 0 0 0 0 x 0 0
0 0 0 0 0 0 0 1 x 0 0
0 0 0 0 0 0 0 0 x 0 0
0 0 0 0 0 0 0 1 x 0 0
0 0 0 0 0 0 0 0 x 0 0
0 0 0 0 0 0 0 1 x 0 0
0 0 0 0 0 0 0 0 x 0 0
0 0 0 0 0 0 0 1 x 0 0
0 0 0 0 0 0 0 0 x 0 0
0 0 0 0 0 0 0 1 x 0 0
0 0 0 0 0 0 0 0 x 0 0
0 0 0 0 0 0 0 1 1 0 0
0 0 0 0 0 0 1 0 1 0 0
0 0 0 0 0 0 1 1 1 0 0
0 0 0 0 0 0 0 0 1 0 0
0 0 0 0 0 0 0 1 1 0 0
0 0 0 0 0 0 0 0 1 0 0
0 0 0 0 0 0 0 1 1 0 0
0 0 0 0 0 0 0 0 1 0 0
0 0 0 0 0 0 0 1 1 0 68
0 0 0 0 0 0 0 0 1 0 68
0 0 0 0 0 0 0 1 1 0 0
0 0 0 0 0 0 0 0 1 0 0
0 0 0 0 0 0 0 1 1 0 0
0 0 0 0 0 0 0 0 1 0 0
0 0 0 0 0 0 0 1 1 0 0
0 0 0 0 0 0 0 0 1 0 0
0 0 0 0 0 0 0 1 1 0 0
0 0 0 0 0 0 0 0 1 0 0
0 0 0 0 0 0 0 1 1 0 0
0 0 0 0 0 0 0 0 1 0 0
0 0 0 0 0 0 0 1 1 0 0
0 0 0 0 0 0 0 0 1 0 0
0 0 0 0 0 0 0 1 1 0 0
0 0 0 0 0 0 0 0 1 0 0
0 0 0 0 0 0 0 1 1 0 0
0 0 0 0 0 0 0 0 1 0 0
0 0 0 0 0 0 0 1 1 0 0
0 0 0 0 0 0 0 0 1 0 0
0 0 0 0 0 0 0 1 1 0 0
0 0 0 0 0 0 0 0 1 0 0
0 0 0 0 0 0 0 1 1 0 0
0 0 0 0 0 0 0 0 1 0 0
0 0 0 0 0 0 0 1 1 0 0
0 0 0 0 0 0 0 0 1 0 0
0 0 0 0 0 0 0 1 1 1 0
0 0 0 0 0 0 0 0 1 1 0
0 0 0 0 0 0 0 1 1 1 0
0 0 0 0 0 0 0 0 1 1 0
0 0 0 0 0 0 0 1 1 1 0
0 0 0 0 0 0 1 0 1 X 0
0 0 0 0 0 0 1 1 1 X 0
0 0 0 0 0 0 0 0 1 0 0
0 0 0 0 0 0 0 1 1 0 0
0 0 0 0 0 0 0 0 1 0 0
0 0 0 0 0 0 0 1 1 0 0
0 0 0 0 0 0 0 0 1 0 0
0 0 0 0 0 0 0 1 1 0 68
0 0 0 0 0 0 0 0 1 0 68
0 0 0 0 0 0 0 1 1 0 0
0 0 0 0 0 0 0 0 1 0 0
0 0 0 0 0 0 0 1 1 0 0
0 0 0 0 0 0 0 0 1 0 0
0 0 0 0 0 0 0 1 1 0 0
0 0 0 0 0 0 0 0 1 0 0
0 0 0 0 0 0 0 1 1 0 0
0 0 0 0 0 0 0 0 1 0 0
0 0 0 0 0 0 0 1 1 0 0
0 0 0 0 0 0 0 0 1 0 0
0 0 0 0 0 0 0 1 1 0 0
0 0 0 0 0 0 0 0 1 0 0
0 0 0 0 0 0 0 1 1 0 0
0 0 0 0 0 0 0 0 1 0 0
0 0 0 0 0 0 0 1 1 0 0
0 0 0 0 0 0 0 0 1 0 0
0 0 0 0 0 0 0 1 1 0 0
0 0 0 0 0 0 0 0 1 0 0
0 0 0 0 0 0 0 1 1 0 0
0 0 0 0 0 0 0 0 1 0 0
0 0 0 0 0 0 0 1 1 0 0
0 0 0 0 0 0 0 0 1 0 0
0 0 0 0 0 0 0 1 1 0 0
0 0 0 0 0 0 0 0 1 0 0
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*/

/* Test case 06_P05T1:
M N progIN reset progLoad start result clk valid done output
0 0 0 0 0 0 0 0 x x x
0 0 0 0 0 0 0 1 x x x
0 0 0 1 0 0 0 0 x x x
0 0 0 1 0 0 0 1 0 0 x
0 0 0 0 0 0 0 0 0 0 x
0 0 0 0 0 0 0 1 0 0 x
0 0 0 0 0 0 0 0 0 0 x
0 0 0 0 0 0 0 1 0 0 x
0 0 0 0 0 0 0 0 0 0 x
0 0 0 0 0 0 0 1 0 0 x
0 0 0 0 0 0 0 0 0 0 x
0 0 0 0 0 0 0 1 0 0 x
0 0 0 0 0 0 0 0 0 0 x
0 0 0 0 0 0 0 1 0 0 x
0 0 0 0 0 0 0 0 0 0 x
0 0 0 0 0 0 0 1 0 0 x
0 0 0 0 0 0 0 0 0 0 x
0 0 0 0 0 0 0 1 0 0 x
0 0 0 0 0 0 0 0 0 0 x
0 0 0 0 0 0 0 1 0 0 x
0 0 0 0 0 0 0 0 0 0 x
0 0 0 0 0 0 0 1 0 0 x
0 0 0 0 0 0 0 0 0 0 x
0 0 0 0 0 0 0 1 0 0 x
0 0 0 0 0 0 0 0 0 0 x
0 0 0 0 0 0 0 1 0 0 x
0 0 0 0 0 0 0 0 0 0 x
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*/

/* Test case t10:
M	N	progIN	reset	progLoad	start	result	clk	valid	done	output
0	0	0	0	0	0	0	0	x	x	x
0	0	0	0	0	0	0	1	x	x	x
0	0	0	1	0	0	0	0	x	x	x
0	0	0	1	0	0	0	1	0	0	0
0	0	0	0	0	0	0	0	0	0	0
0	0	0	0	0	0	0	1	0	0	0
0	0	0	0	0	0	0	0	0	0	0
0	0	0	0	0	0	0	1	0	0	0
0	0	0	0	0	0	0	0	0	0	0
0	0	0	0	0	0	0	1	0	0	0
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*/

/* Test case 03_P02T2:
M N progIN reset progLoad start result clk valid done output
0 0 0 0 0 0 0 0 x x x
0 0 0 0 0 0 0 1 x x x
0 0 0 1 0 0 0 0 x x x
0 0 0 1 0 0 0 1 0 0 0
0 0 0 0 0 0 0 0 0 0 0
0 0 0 0 0 0 0 1 0 0 0
0 0 0 0 0 0 0 0 0 0 0
0 0 0 0 0 0 0 1 0 0 0
0 0 0 0 0 0 0 0 0 0 0
0 0 0 0 0 0 0 1 0 0 0
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*/

/* Test case 07_P06T1:
M N progIN reset progLoad start result clk valid done output
0 0 0 0 0 0 0 0 x x x
0 0 0 0 0 0 0 1 x x x
0 0 0 1 0 0 0 0 x x x
0 0 0 1 0 0 0 1 0 0 x
0 0 0 0 0 0 0 0 0 0 x
0 0 0 0 0 0 0 1 0 0 x
0 0 0 0 0 0 0 0 0 0 x
0 0 0 0 0 0 0 1 0 0 x
0 0 0 0 0 0 0 0 0 0 x
0 0 0 0 0 0 0 1 0 0 x
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*/

/* Test case t12:
M	N	progIN	reset	progLoad	start	result	clk	valid	done	output
0	0	0	0	0	0	0	0	x	x	x
0	0	0	0	0	0	0	1	x	x	x
0	0	0	1	0	0	0	0	x	x	x
0	0	0	1	0	0	0	1	0	0	x
0	0	0	0	0	0	0	0	0	0	x
0	0	0	0	0	0	0	1	0	0	x
0	0	0	0	0	0	0	0	0	0	x
0	0	0	0	0	0	0	1	0	0	x
0	0	0	0	0	0	0	0	0	0	x
0	0	0	0	0	0	0	1	0	0	x
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*/

/* Test case 04_P03T2:
M N progIN reset progLoad start result clk valid done output
0 0 0 0 0 0 0 0 x x x
0 0 0 0 0 0 0 1 x x x
0 0 0 1 0 0 0 0 x x x
0 0 0 1 0 0 0 1 0 0 x
0 0 0 0 0 0 0 0 0 0 x
0 0 0 0 0 0 0 1 0 0 x
0 0 0 0 0 0 0 0 0 0 x
0 0 0 0 0 0 0 1 0 0 x
0 0 0 0 0 0 0 0 0 0 x
0 0 0 0 0 0 0 1 0 0 x
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*/

/* Test case 08_P06T2:
M N progIN reset progLoad start result clk valid done output
0 0 0 0 0 0 0 0 x x x
0 0 0 0 0 0 0 1 x x x
0 0 0 1 0 0 0 0 x x x
0 0 0 1 0 0 0 1 0 0 x
0 0 0 0 0 0 0 0 0 0 x
0 0 0 0 0 0 0 1 0 0 x
0 0 0 0 0 0 0 0 0 0 x
0 0 0 0 0 0 0 1 0 0 x
0 0 0 0 0 0 0 0 0 0 x
0 0 0 0 0 0 0 1 0 0 x
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*/

/* Test case t14:
M	N	progIN	reset	progLoad	start	result	clk	valid	done	output
0	0	0	0	0	0	0	0	x	x	x
0	0	0	0	0	0	0	1	x	x	x
0	0	0	1	0	0	0	0	x	x	x
0	0	0	1	0	0	0	1	0	0	x
0	0	0	0	0	0	0	0	0	0	x
0	0	0	0	0	0	0	1	0	0	x
0	0	0	0	0	0	0	0	0	0	x
0	0	0	0	0	0	0	1	0	0	x
0	0	0	0	0	0	0	0	0	0	x
0	0	0	0	0	0	0	1	0	0	x
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*/
